# Fritzing sketch FrtizsBox (saved by Fritzing 0.9.3b)
breadboards: 1

parts:
  Part2 = PowerBoost 500 Charger
  Battery = LIPO-110mAh [package=lipo-110]
  R_Red = Resistor [tolerance=±5% resistance=120 package="0402 [SMD]"]
  R_Green = Resistor [tolerance=±5% resistance=68 package="0402 [SMD]"]
  R_Blue = Resistor [tolerance=±5% resistance=68 package="0402 [SMD]"]
  SP1 = SPEAKER [package=pcb_mount_speaker]
  SP2 = SPEAKER [package=pcb_mount_speaker]
  Part1 = Arduino Pro Mini (5V)
  R5 = Resistor [tolerance=±5% resistance=1k package="1206 [SMD]"]
  DFRobot_DFPlayer_Mini1 = DFRobot DFPlayer Mini [part_number=DFR0299]
  4x3_Keypad = 3x4 Keypad
  R_Switch_Pulldown = Resistor [tolerance=±5% resistance=10k package=THT]
  Part3 = Audio Jack Breakout
  PWR_Arduino = female pin header, 2 pins [form="♀ (female)"]
  To_DFPlayer = male pin header, 2 pins [form="♂ (male)"]
  PWR_Encoder = female pin header, 2 pins [form="♀ (female)"]
  Serial_DFPlayer = female pin header, 2 pins [form="♀ (female)"]
  PWR_DFPlayer = female pin header, 2 pins [form="♀ (female)"]
  RGB_LED = female pin header, 3 pins [form="♀ (female)"]
  To_RGB_LED = male pin header, 3 pins [form="♂ (male)"]
  Data_Encoder+Switch = female pin header, 3 pins [form="♀ (female)"]
  To_Encoder_&_Switch = male pin header, 3 pins [form="♂ (male)"]
  VCC = female pin header, 4 pins [form="♀ (female)"]
  GND = female pin header, 4 pins [form="♀ (female)"]
  PWR_Keypad = male pin header, 2 pins [form="♂ (male)"]
  Encoder = ENCODER_RGB_CA [package=encoder_led_3]
  On_Off = SPST Switch [package=switch-spdt_kit]
  R6 = Resistor [tolerance=±5% resistance=680 package="2010 [SMD]"]
  R7 = Resistor [tolerance=±5% resistance=680 package="2010 [SMD]"]
  U1 = Mono 2.6W Class D Amplifier [package=8-tdfn-ep]

nets:
  N1: Part2.GND_BAT_IN, Battery.-
  N2: Part2.VBAT_IN, Battery.+
  N3: Part2.ENABLE, On_Off.O
  N4: Part2.GND, GND.pin1, GND.pin2, GND.pin3, GND.pin4, On_Off.P
  N5: Part2.5.0V, VCC.pin1, VCC.pin2, VCC.pin3, VCC.pin4
  N6: R_Red.Pin_0, Encoder.-R
  N7: R_Red.Pin_1, RGB_LED.pin1
  N8: R_Green.Pin_0, Encoder.-G
  N9: R_Green.Pin_1, RGB_LED.pin2
  N10: R_Blue.Pin_0, Encoder.-B
  N11: R_Blue.Pin_1, RGB_LED.pin3
  GND: SP1.+, DFRobot_DFPlayer_Mini1.GND-1, DFRobot_DFPlayer_Mini1.GND-2, Part3.GND, PWR_DFPlayer.pin1, U1.IN-, U1.GND
  N12: SP1.-, U1.VDD
  N13: SP2.+, U1.OUT+
  N14: SP2.-, U1.OUT-
  N15: Part1.VCC, PWR_Arduino.pin2
  N16: Part1.GND, PWR_Arduino.pin1
  N17: Part1.A0, 4x3_Keypad.DATA
  N18: Part1.D9, To_RGB_LED.pin1
  N19: Part1.D8, To_DFPlayer.pin1
  N20: Part1.D7, To_DFPlayer.pin2
  N21: Part1.D6, To_RGB_LED.pin2
  N22: Part1.D5, To_RGB_LED.pin3
  N23: Part1.D4, To_Encoder_&_Switch.pin1
  N24: Part1.D3, To_Encoder_&_Switch.pin2
  N25: Part1.D2, To_Encoder_&_Switch.pin3
  N26: R5.Pin_0, Serial_DFPlayer.pin1
  N27: R5.Pin_1, DFRobot_DFPlayer_Mini1.TX
  N28: DFRobot_DFPlayer_Mini1.VCC, PWR_DFPlayer.pin2, U1.GAIN
  N29: DFRobot_DFPlayer_Mini1.RX, Serial_DFPlayer.pin2
  N30: DFRobot_DFPlayer_Mini1.DAC_R, R7.Pin_1
  N31: DFRobot_DFPlayer_Mini1.DAC_L, R6.Pin_1
  N32: 4x3_Keypad.GND, PWR_Keypad.pin2
  N33: 4x3_Keypad.VCC, PWR_Keypad.pin1
  N34: R_Switch_Pulldown.Pin_0, PWR_Encoder.pin1, Encoder.C
  N35: R_Switch_Pulldown.Pin_1, Data_Encoder+Switch.pin1, Encoder.SW
  N36: Part3.RING_SHUNT, U1.IN+
  N37: Part3.RING, R7.Pin_0
  N38: Part3.TIP_SHUNT, U1.SHDN
  N39: Part3.TIP, R6.Pin_0
  N40: PWR_Encoder.pin2, Encoder.+
  N41: Data_Encoder+Switch.pin2, Encoder.A
  N42: Data_Encoder+Switch.pin3, Encoder.B

// code stored in the sketch: Hoerbert.ino
#include <SoftwareSerial.h>
#include "DFMiniMp3.h"
#include "MP3Notify.h"
#include "Keypad.h"
#include "Context.h"

// Encoder Pin C = GND
int encoderPinB = 3; // D2 - IRQ0
int encoderPinA = 2; // D3 - IRQ1
int encoderSwitchPin = 4; // D4 //push button switch

//int ledRPin = 9; // D9 PWM
//int ledGPin = 6; // D6 PWM
int ledBPin = 5; // D5 PWM

int mp3RXPin = 7; // D7
int mp3TXPin = 8; // D8

int keypadPin = 14; // A0


// Ecoder Vars
volatile int lastEncoded = 0;
volatile long encoderValue = 0;
long lastencoderValue = 0;
int lastMSB = 0;
int lastLSB = 0;

// App Vars
Context context;
int lastEncoderValue = 0;
int lastKeypadPressed = 0;
boolean lastEncoderSwitchPressed = false;
int volume = 20; // 0 - 30


SoftwareSerial mp3Serial(mp3RXPin, mp3TXPin);
DFMiniMp3<SoftwareSerial, Mp3Notify> mp3(mp3Serial);

void setup() {
  /// MP3 Pins
  pinMode(mp3TXPin, OUTPUT);
  pinMode(mp3RXPin, INPUT);
  setVolume(0);

  context.mp3 = &mp3;
  mp3.begin(&context);
  mp3.setEq(DfMp3_Eq_Pop);
  mp3.enableDAC();
  setVolume(0);

  /// 
  Serial.begin(115200);
  Serial.println(F("initializing..."));

  // First, set all the pins

  /// Encoder Pins
  pinMode(encoderPinA, INPUT);
  pinMode(encoderPinB, INPUT);
  digitalWrite(encoderPinA, HIGH); //turn pullup resistor on
  digitalWrite(encoderPinB, HIGH); //turn pullup resistor on
  //call updateEncoder() when any high/low changed seen
  //on interrupt 0 (pin 2), or interrupt 1 (pin 3)
  attachInterrupt(0, updateEncoder, CHANGE);
  attachInterrupt(1, updateEncoder, CHANGE);

  pinMode(encoderSwitchPin, INPUT);
  digitalWrite(encoderSwitchPin, HIGH); //turn pullup resistor on

  /// LED Pins
//  pinMode(ledRPin, OUTPUT);
//  pinMode(ledGPin, OUTPUT);
  pinMode(ledBPin, OUTPUT);

  /// Keypad Pin
  pinMode(keypadPin, INPUT);

  Serial.println(F("Setup done..."));

  Serial.println(F("Scanning track counts"));
  Serial.print(F("Total track count: "));
  Serial.println(mp3.getTotalTrackCount());
  
  for (int i = 1; i <= 12; i++) {
    // Folders are 1-indexed for `getFolderTrackCount`
    context.tracksInFolders[i] = mp3.getFolderTrackCount(i);
  }

  for (int i = 1; i <= 12; i++) {
    Serial.print(F("Folder "));
    Serial.print(i);
    Serial.print(F(" has: "));
    Serial.println(context.tracksInFolders[i]); //read fill counts in folder SD:/i
  }

  // light it up!
  setVolume(volume);
}

void loop() {
  //Do stuff here
  boolean encoderSwitchPressed = digitalRead(encoderSwitchPin);
  if (encoderSwitchPressed) {
    //button is not being pushed
    if (!lastEncoderSwitchPressed) {
      Serial.println(F("Pushed"));
      togglePlayPause(&context);
    }
  } else {
    //button is being pushed
  }
  lastEncoderSwitchPressed = encoderSwitchPressed;

  updateVolume();

  int keypadPressed = CheckButtons(keypadPin);

  if (keypadPressed != lastKeypadPressed) {
    lastKeypadPressed = keypadPressed;

    if (keypadPressed > 0) {
      Serial.print(F("Taste: "));
      Serial.println(keypadPressed);
      int folder = folderForKeypadButton(keypadPressed);
      int track = 1;
      if (folder == context.currentFolder) {
        playNextTrack(&context);
      } else {
        playFolderAndTrack(folder, track, &context);
      }
    }
  }

  waitMilliseconds(50);
}

int folderForKeypadButton(int button) {
  switch(button) {
    case 1:  return 4;
    case 2:  return 8;
    case 3:  return 12;
    case 4:  return 3;
    case 5:  return 7;
    case 6:  return 11;
    case 7:  return 2;
    case 8:  return 6;
    case 9:  return 10;
    case 10: return 1;
    case 11: return 5;
    case 12: return 9;
  }
}


void waitMilliseconds(uint16_t msWait) {
  uint32_t start = millis();
  while ((millis() - start) < msWait) {
    // calling mp3.loop() periodically allows for notifications
    // to be handled without interrupts
    mp3.loop();

    delay(1);
  }
}

void setVolume(int volume) {
//    mp3.setVolume(volume);
//    Serial.print(F("Setting volume to "));
//    Serial.println(volume);
    setLEDColor(255-PWMValueForVolumne(volume), PWMValueForVolumne(volume), PWMValueForVolumne(volume));
}

void updateVolume() {
  if (lastEncoderValue != encoderValue) {
    Serial.println(lastEncoderValue);
    int encoderDiff = encoderValue - lastEncoderValue;
    lastEncoderValue = encoderValue;
    volume += encoderDiff/3;
    volume = max(0, min(30, volume));

    setVolume(volume);
  }
}

void setLEDColor(int red, int green, int blue) {
  // Adjust for common anode
  red = 255 - max(0, min(255, red));
  green = 255 - max(0, min(255, green));
  blue = 255 - max(0, min(255, blue));

//  analogWrite(ledRPin, red);
//  analogWrite(ledGPin, green);
  analogWrite(ledBPin, blue);
}

int PWMValueForVolumne(int input) {
if (input <=   0 ) return  0 ;
if (input ==  1 ) return  1 ;
if (input ==  2 ) return  2 ;
if (input ==  3 ) return  3 ;
if (input ==  4 ) return  4 ;
if (input ==  5 ) return  5 ;
if (input ==  6 ) return  6 ;
if (input ==  7 ) return  7 ;
if (input ==  8 ) return  8 ;
if (input ==  9 ) return  9 ;
if (input ==  10  ) return  10  ;
if (input ==  11  ) return  13  ;
if (input ==  12  ) return  17  ;
if (input ==  13  ) return  21  ;
if (input ==  14  ) return  26  ;
if (input ==  15  ) return  32  ;
if (input ==  16  ) return  39  ;
if (input ==  17  ) return  47  ;
if (input ==  18  ) return  56  ;
if (input ==  19  ) return  65  ;
if (input ==  20  ) return  76  ;
if (input ==  21  ) return  88  ;
if (input ==  22  ) return  101 ;
if (input ==  23  ) return  115 ;
if (input ==  24  ) return  131 ;
if (input ==  25  ) return  148 ;
if (input ==  26  ) return  166 ;
if (input ==  27  ) return  186 ;
if (input ==  28  ) return  208 ;
if (input ==  29  ) return  231 ;
if (input >=  30  ) return  255 ;
}


void updateEncoder() {
  int MSB = digitalRead(encoderPinA); //MSB = most significant bit
  int LSB = digitalRead(encoderPinB); //LSB = least significant bit

  int encoded = (MSB << 1) | LSB; //converting the 2 pin value to single number
  int sum  = (lastEncoded << 2) | encoded; //adding it to the previous encoded value

  if (sum == 0b1101 || sum == 0b0100 || sum == 0b0010 || sum == 0b1011) encoderValue ++;
  if (sum == 0b1110 || sum == 0b0111 || sum == 0b0001 || sum == 0b1000) encoderValue --;

  lastEncoded = encoded; //store this value for next time
}
